# Fritzing sketch fifider (saved by Fritzing 0.9.2b)
circuit board: 11.5cm x 9cm
breadboards: 1

parts:
  C2 = Ceramic Capacitor [capacitance=100nF package="100 mil [THT, multilayer]"]
  R12 = Resistor [tolerance=±5% resistance=10k package=THT]
  R13 = Resistor [tolerance=±5% resistance=10k package=THT]
  R14 = Resistor [tolerance=±5% resistance=10k package=THT]
  R15 = Resistor [tolerance=±5% resistance=10k package=THT]
  R16 = Resistor [tolerance=±5% resistance=10k package=THT]
  J10 = female pin header, 2 pins [form="♀ (female)"]
  J11 = female pin header, 2 pins [form="♀ (female)"]
  J12 = female pin header, 2 pins [form="♀ (female)"]
  U5 = 74HC595 [part_number=IC1 package="DIP16 [THT]"]
  U6 = 74HC595 [part_number=IC2 package="DIP16 [THT]"]
  R17 = Resistor [tolerance=±5% resistance=10k package=THT]
  R18 = Resistor [tolerance=±5% resistance=10k package=THT]
  R19 = Resistor [tolerance=±5% resistance=10k package=THT]
  R20 = Resistor [tolerance=±5% resistance=10k package=THT]
  LED4 = LED - 3mm [color="Yellow (592nm)" package="3 mm [THT]"]
  LED5 = LED - 3mm [color="Red (633nm)" package="3 mm [THT]"]
  LED6 = LED - 3mm [color="Red (633nm)" package="3 mm [THT]"]
  J13 = male pin header, 12 pins [form="♂ (male)"]
  IC2 = IC, DIP package, 16 pins [chip_label=IC]
  J15 = female pin header, 1 pin [form="♀ (female)"]
  J16 = female pin header, 1 pin [form="♀ (female)"]
  J9 = female pin header, 2 pins [form="♀ (female)"]
  J14 = male pin header, 7 pins [form="♂ (male)"]

nets:
  N1: C2.0, U5.ST_CP, U6.ST_CP, J14.pin2
  GND: C2.1, J10.pin2, J11.pin2, J12.pin2, U5.GND, U5.OE, U6.GND, U6.OE, J15.pin1, J9.pin2
  N2: R12.Pin_0, IC2.pin11
  N3: R12.Pin_1, U5.Q4
  N4: R13.Pin_0, IC2.pin13
  N5: R13.Pin_1, U5.Q3
  N6: R14.Pin_0, IC2.pin12
  N7: R14.Pin_1, U5.Q2
  N8: R15.Pin_0, IC2.pin10
  N9: R15.Pin_1, U5.Q1
  N10: R16.Pin_0, IC2.pin9
  N11: R16.Pin_1, U5.Q0
  N12: J10.pin1, R19.Pin_1, J14.pin5
  N13: J11.pin1, R18.Pin_1, J14.pin6
  N14: J12.pin1, R20.Pin_1, J14.pin4
  5V: U5.MR, U5.VCC, U6.MR, U6.VCC, R17.Pin_0, R18.Pin_0, R19.Pin_0, R20.Pin_0, J16.pin1
  N15: U5.SH_CP, U6.SH_CP, J14.pin3
  N16: U5.DS, U6.Q7'
  N17: U6.Q1, LED4.cathode, J13.pin11
  N18: U6.Q2, LED5.cathode, J13.pin10
  N19: U6.Q3, J13.pin9
  N20: U6.Q4, J13.pin8
  N21: U6.Q5, J13.pin7
  N22: U6.Q6, J13.pin6
  N23: U6.DS, J14.pin1
  N24: U6.Q0, LED6.cathode, J13.pin12
  N25: R17.Pin_1, J9.pin1, J14.pin7
  N26: LED4.anode, LED5.anode, LED6.anode, J13.pin5, IC2.pin8
  N27: J13.pin1, IC2.pin4
  N28: J13.pin2, IC2.pin5
  N29: J13.pin3, IC2.pin6
  N30: J13.pin4, IC2.pin7
